// Logisim project IDEX_Pipeline_Registers.circ as structural Verilog: 1 circuit, main circuit main
// RegDst
module main (
  input  RegDst,
  input  Branch,
  input  MemRead,
  input  MemToReg,
  input  [3:0] ALUOp,
  input  MemWrite,
  input  ALUSrc,
  input  RegWrite,
  input  Clock,
  input  Reset,
  output [1:0] WB,
  output [2:0] M,
  output RegDst_2,
  output [3:0] ALUOp_2,
  output ALUSrc_2
);

  Register #(.width(1)) u_RegDst (.D(RegDst), .Q(RegDst_2), .clk(Clock), .clr(Reset));  // open: en
  Register #(.width(1)) u_MemRead (.D(MemRead), .Q(M[0]), .clk(Clock), .clr(Reset));  // open: en
  Register #(.width(4)) u_ALUOp (.D(ALUOp), .Q(ALUOp_2), .clk(Clock), .clr(Reset));  // open: en
  Register #(.width(1)) u_ALUSrc (.D(ALUSrc), .Q(ALUSrc_2), .clk(Clock), .clr(Reset));  // open: en
  Register #(.width(1)) u_Branch (.D(Branch), .Q(M[2]), .clk(Clock), .clr(Reset));  // open: en
  Register #(.width(1)) u_MemToReg (.D(MemToReg), .Q(WB[1]), .clk(Clock), .clr(Reset));  // open: en
  Register #(.width(1)) u_MemWrite (.D(MemWrite), .Q(M[1]), .clk(Clock), .clr(Reset));  // open: en
  Register #(.width(1)) u_RegWrite (.D(RegWrite), .Q(WB[0]), .clk(Clock), .clr(Reset));  // open: en

  // Notes on the sheet:
  //   Inputs
  //   ID/EX Pipeline Registers
  //   Outputs
endmodule
