// Logisim project control.circ as structural Verilog: 3 circuits, main circuit ALUcontrol_0
module ALUcontrol_0 (
  input  ALUop_1,
  input  ALUop_0,
  input  F5,
  input  F4,
  input  F3,
  input  F2,
  input  F1,
  input  F0,
  output Operation_3,
  output Operation_2,
  output Operation_1,
  output Operation_0
);
endmodule

module Control_0 (
  input  op_5,
  input  op_4,
  input  op_3,
  input  op_2,
  input  op_1,
  input  op_0,
  output RegDst,
  output Branch,
  output MemRead,
  output MemToReg,
  output MemWrite,
  output ALUsrc,
  output RegWrite
);
endmodule

module Control_1 (
  input  op_5,
  input  op_4,
  input  op_3,
  input  op_2,
  input  op_1,
  input  op_0,
  output ALUop_1,
  output ALUop_0
);
endmodule
