// Logisim project datapathtest.circ as structural Verilog: 16 circuits, main circuit Datapath
// Read Data 2
module Datapath (
  input  Clear,
  input  Reset
);

  wire and_2_out, and_3_out, Clock_out, Control_alusrc, Control_branch, Control_memread, Control_memtoreg,
       Control_memwrite, Control_regdst, Control_regwrite, EX_MEM_branch, EX_MEM_memread, EX_MEM_memwrite,
       ID_EX_alusrc_2, ID_EX_regdst_2, MEM_WB_memtoreg, MEM_WB_regwrite, not_1_out, registerfile_1_p2,
       splitter_01_1_out_2;
  wire [1:0] EX_MEM_wb_2, ID_EX_wb;
  wire [2:0] ID_EX_m;
  wire [3:0] ALU_Control_operation, Control_aluop, ID_EX_aluop_2;
  wire [4:0] instructiondecode_1_rd, instructiondecode_1_rs, instructiondecode_1_rt,
       instructiondecode_1_shamt, multiplexer_2_out, rd_q, registerfile_1_p4, rt_q, shamt_q, Write_Reg_q;
  wire [5:0] funct_q, instructiondecode_1_funct, instructiondecode_1_op;
  wire [15:0] instructiondecode_1_immediate;
  wire [19:0] Address_wordaddress;
  wire [31:0] _32_bit_Address_q, adder_1_out, ALU_Result_2_q, ALU_Result_q, Branch_Address_q,
       Branch_branchaddress, Instruction_q, memorydata_1_readdata, mips_alu_1_p5, mips_ram_1_p7,
       mipsprogramrom_1_p2, multiplexer_1_out, multiplexer_3_out, PC_4_2_q, PC_4_q, Read_Data_1_q,
       Read_Data_2_2_q, Read_Data_2_q, register_1_q, register_2_q, registerfile_1_p1, registerfile_1_p7,
       registerfile_1_p8, Sign_extend_out_2, wirewidthext_2_1_wordaddress, Write_Data_q;

  Clock Clock (.out(Clock_out));
  WireWidthExt_2 wirewidthext_2_1 (
    .ByteAddress(register_1_q), .WordAddress(wirewidthext_2_1_wordaddress));  // open: Unaligned
  Multiplexer #(.width(32), .enable("false")) multiplexer_1 (
    .in0(adder_1_out), .in1(Branch_Address_q), .out(multiplexer_1_out), .sel(and_2_out));
  Register #(.width(32)) register_1 (
    .D(multiplexer_1_out), .Q(register_1_q), .clk(Clock_out), .clr(Reset));  // open: en
  Adder #(.width(32)) adder_1 (.a(32'h4), .b(register_1_q), .out(adder_1_out));  // open: cin, cout
  // MIPSProgramROM mipsprogramrom_1: pin names not known; wires that end beside it: wirewidthext_2_1_wordaddress, mipsprogramrom_1_p2
  Register #(.width(32)) PC_4 (.D(adder_1_out), .Q(PC_4_q), .clk(Clock_out), .clr(Reset));  // open: en
  InstructionDecode instructiondecode_1 (
    .Instruction(Instruction_q), .op(instructiondecode_1_op), .rs(instructiondecode_1_rs),
    .rt(instructiondecode_1_rt), .rd(instructiondecode_1_rd), .shamt(instructiondecode_1_shamt),
    .funct(instructiondecode_1_funct), .immediate(instructiondecode_1_immediate));  // open: address
  Register #(.width(32)) Instruction (
    .D(mipsprogramrom_1_p2), .Q(Instruction_q), .clk(Clock_out), .clr(Reset));  // open: en
  Control Control (
    .op(instructiondecode_1_op), .RegDst(Control_regdst), .Branch(Control_branch), .MemRead(Control_memread),
    .MemToReg(Control_memtoreg), .ALUop(Control_aluop), .MemWrite(Control_memwrite), .ALUsrc(Control_alusrc),
    .RegWrite(Control_regwrite));
  not not_1 (not_1_out, Clock_out);
  // RegisterFile registerfile_1: pin names not known; wires that end beside it: registerfile_1_p1, registerfile_1_p2, registerfile_1_p2, registerfile_1_p4, instructiondecode_1_rs, instructiondecode_1_rt, registerfile_1_p7, registerfile_1_p8
  SignExtend Sign_extend (.in_1(instructiondecode_1_immediate), .out_2(Sign_extend_out_2));
  and and_1 (registerfile_1_p2, MEM_WB_regwrite, not_1_out);
  IDEX_Pipeline_Registers ID_EX (
    .RegDst(Control_regdst), .Branch(Control_branch), .MemRead(Control_memread), .MemToReg(Control_memtoreg),
    .ALUOp(Control_aluop), .MemWrite(Control_memwrite), .ALUSrc(Control_alusrc), .RegWrite(Control_regwrite),
    .Clock(Clock_out), .Reset(Reset), .WB(ID_EX_wb), .M(ID_EX_m), .RegDst_2(ID_EX_regdst_2),
    .ALUOp_2(ID_EX_aluop_2), .ALUSrc_2(ID_EX_alusrc_2));
  Register #(.width(32)) PC_4_2 (.D(PC_4_q), .Q(PC_4_2_q), .clk(Clock_out), .clr(Reset));  // open: en
  Register #(.width(32)) Read_Data_1 (
    .D(registerfile_1_p7), .Q(Read_Data_1_q), .clk(Clock_out), .clr(Reset));  // open: en
  Register #(.width(32)) Read_Data_2 (
    .D(registerfile_1_p8), .Q(Read_Data_2_q), .clk(Clock_out), .clr(Reset));  // open: en
  Register #(.width(32)) _32_bit_Address (
    .D(Sign_extend_out_2), .Q(_32_bit_Address_q), .clk(Clock_out), .clr(Reset));  // open: en
  Register #(.width(6)) funct (.D(instructiondecode_1_funct), .Q(funct_q), .clk(Clock_out), .clr(Reset));  // open: en
  Register #(.width(5)) shamt (.D(instructiondecode_1_shamt), .Q(shamt_q), .clk(Clock_out), .clr(Reset));  // open: en
  Register #(.width(5)) rt (.D(instructiondecode_1_rt), .Q(rt_q), .clk(Clock_out), .clr(Reset));  // open: en
  Register #(.width(5)) rd (.D(instructiondecode_1_rd), .Q(rd_q), .clk(Clock_out), .clr(Reset));  // open: en
  Multiplexer #(.width(5), .enable("false")) multiplexer_2 (
    .in0(rt_q), .in1(rd_q), .out(multiplexer_2_out), .sel(ID_EX_regdst_2));
  ALUcontrol ALU_Control (.funct(funct_q), .ALUop(ID_EX_aluop_2), .Operation(ALU_Control_operation));
  Multiplexer #(.width(32), .enable("false")) multiplexer_3 (
    .in0(Read_Data_2_q), .in1(_32_bit_Address_q), .out(multiplexer_3_out), .sel(ID_EX_alusrc_2));
  // Mips_ALU mips_alu_1: pin names not known; wires that end beside it: Read_Data_1_q, multiplexer_3_out, ALU_Control_operation, shamt_q, mips_alu_1_p5
  EXMEM_Pipeline_Registers EX_MEM (
    .WB(ID_EX_wb), .M(ID_EX_m), .Clock(Clock_out), .Reset(Reset), .WB_2(EX_MEM_wb_2),
    .MemRead(EX_MEM_memread), .MemWrite(EX_MEM_memwrite), .Branch(EX_MEM_branch));
  BranchAddress Branch (.PC_4(PC_4_2_q), .Address(_32_bit_Address_q), .BranchAddress(Branch_branchaddress));
  Register #(.width(32)) Branch_Address (
    .D(Branch_branchaddress), .Q(Branch_Address_q), .clk(Clock_out), .clr(Reset));  // open: en
  Register #(.width(32)) ALU_Result (.D(mips_alu_1_p5), .Q(ALU_Result_q), .clk(Clock_out), .clr(Reset));  // open: en
  Register #(.width(32)) Read_Data_2_2 (
    .D(Read_Data_2_q), .Q(Read_Data_2_2_q), .clk(Clock_out), .clr(Reset));  // open: en
  Register #(.width(32)) Write_Data (.D(Read_Data_2_q), .Q(Write_Data_q), .clk(Clock_out), .clr(Reset));  // open: en
  Register #(.width(5)) Write_Reg (.D(multiplexer_2_out), .Q(Write_Reg_q), .clk(Clock_out), .clr(Reset));  // open: en
  and and_2 (and_2_out, EX_MEM_branch, splitter_01_1_out_2);
  Splitter_01 splitter_01_1 (.in_1(ALU_Result_q), .out_2(splitter_01_1_out_2));
  WireWidthExt Address (.ByteAddress(ALU_Result_q), .WordAddress(Address_wordaddress));
  and and_3 (and_3_out, not_1_out, EX_MEM_memwrite);
  // MIPS_RAM mips_ram_1: pin names not known; wires that end beside it: Address_wordaddress, Write_Data_q, 4'b1111, and_3_out, EX_MEM_memread, Clear, mips_ram_1_p7
  MemoryData memorydata_1 (
    .WriteData(Read_Data_2_2_q), .FromMemory(mips_ram_1_p7), .Write(EX_MEM_memwrite), .Read(EX_MEM_memread),
    .ReadData(memorydata_1_readdata), .ToMemory(mips_ram_1_p7));
  MEMWB_Pipeline_Registers MEM_WB (
    .WB(EX_MEM_wb_2), .Clock(Clock_out), .Reset(Reset), .RegWrite(MEM_WB_regwrite), .MemToReg(MEM_WB_memtoreg));
  Register #(.width(32)) ALU_Result_2 (.D(ALU_Result_q), .Q(ALU_Result_2_q), .clk(Clock_out), .clr(Reset));  // open: en
  Register #(.width(32)) register_2 (
    .D(memorydata_1_readdata), .Q(register_2_q), .clk(Clock_out), .clr(Reset));  // open: en
  Register #(.width(5)) Write_Reg_2 (.D(Write_Reg_q), .Q(registerfile_1_p4), .clk(Clock_out), .clr(Reset));  // open: en
  Multiplexer #(.width(32), .enable("false")) multiplexer_4 (
    .in0(ALU_Result_2_q), .in1(register_2_q), .out(registerfile_1_p1), .sel(MEM_WB_memtoreg));

  // Notes on the sheet:
  //   PCSrc
  //   IF
  //   Instruction Memory
  //   PC
  //   IF/ID
  //   IF/ID
  //   Clock
  //   PCSrc
  //   Branch Address
  //   ID
  //   Address: 10:6
  //   Write Data
  //   Registers
  //   Address: 15:0
  //   RegWrite
  //   Write Register
  //   Address: 20:16
  //   Address: 15:11
  //   ID/EX
  //   ID/EX
  //   ID/EX
  //   ID/EX
  //   ID/EX
  //   ID/EX
  //   ID/EX
  //   ID/EX
  //   RegDst
  //   EX
  //   RegWrite
  //   Sign-extended Address
  //   Data Memory
  //   !Clock
  //   Write Register
  //   ALU
  //   EX/MEM
  //   EX/MEM
  //   EX/MEM
  //   EX/MEM
  //   Branch
  //   MEM
  //   PCSrc
  //   MemRead
  //   PCSrc
  //   MemRead
  //   MemWrite
  //   RegWrite
  //   MEM/WB
  //   MEM/WB
  //   MEM/WB
  //   WB
  //   MemToReg
endmodule

module Control (
  input  [5:0] op,
  output RegDst,
  output Branch,
  output MemRead,
  output MemToReg,
  output [3:0] ALUop,
  output MemWrite,
  output ALUsrc,
  output RegWrite
);

  control_0 control_0_1 (
    .op_5(op[5]), .op_4(op[4]), .op_3(op[3]), .op_2(op[2]), .op_1(op[1]), .op_0(op[0]), .RegDst(RegDst),
    .Branch(Branch), .MemRead(MemRead), .MemToReg(MemToReg), .MemWrite(MemWrite), .ALUsrc(ALUsrc),
    .RegWrite(RegWrite));
  control_1 control_1_1 (
    .op_5(op[5]), .op_4(op[4]), .op_3(op[3]), .op_2(op[2]), .op_1(op[1]), .op_0(op[0]), .ALUop_3(ALUop[3]),
    .ALUop_2(ALUop[2]), .ALUop_1(ALUop[1]), .ALUop_0(ALUop[0]));
endmodule

module ALUcontrol (
  input  [5:0] funct,
  input  [3:0] ALUop,
  output [3:0] Operation
);

  ALUcontrol_0 alucontrol_0_1 (
    .ALUop_3(ALUop[3]), .ALUop_2(ALUop[2]), .ALUop_1(ALUop[1]), .ALUop_0(ALUop[0]), .F5(funct[5]),
    .F4(funct[4]), .F3(funct[3]), .F2(funct[2]), .F1(funct[1]), .F0(funct[0]), .Operation_3(Operation[3]),
    .Operation_2(Operation[2]), .Operation_1(Operation[1]), .Operation_0(Operation[0]));
endmodule

module WireWidthExt (
  input  [31:0] ByteAddress,
  output [19:0] WordAddress
);


  assign WordAddress = {{10{1'b0}}, ByteAddress[9:0]};
endmodule

module WireWidthExt_2 (
  input  [31:0] ByteAddress,
  output Unaligned,
  output [31:0] WordAddress
);

  nor nor_1 (Unaligned, ByteAddress[0], ByteAddress[1]);

  assign WordAddress = {{22{1'b0}}, ByteAddress[9:2], 2'b00};
endmodule

module ALUcontrol_0 (
  input  ALUop_3,
  input  ALUop_2,
  input  ALUop_1,
  input  ALUop_0,
  input  F5,
  input  F4,
  input  F3,
  input  F2,
  input  F1,
  input  F0,
  output Operation_3,
  output Operation_2,
  output Operation_1,
  output Operation_0
);

  wire and_1_out, and_2_out, and_3_out, and_4_out, and_5_out, and_6_out, and_7_out, and_8_out, and_9_out,
       and_10_out, and_11_out, not_1_out, not_2_out, not_3_out, not_4_out, not_5_out, not_6_out, not_7_out,
       not_8_out, not_9_out, not_10_out;

  and and_1 (and_1_out, ALUop_3, F5, F2);
  and and_2 (and_2_out, ALUop_2, ALUop_0);
  and and_3 (and_3_out, ALUop_3, F1);
  and and_4 (and_4_out, ALUop_3, ALUop_0);
  not not_1 (not_1_out, ALUop_3);
  not not_2 (not_2_out, ALUop_0);
  not not_3 (not_3_out, ALUop_0);
  not not_4 (not_4_out, ALUop_0);
  not not_5 (not_5_out, F5);
  not not_6 (not_6_out, F4);
  not not_7 (not_7_out, F1);
  not not_8 (not_8_out, ALUop_2);
  not not_9 (not_9_out, ALUop_1);
  not not_10 (not_10_out, F5);
  or or_1 (Operation_3, ALUop_0, ALUop_2, and_1_out);
  or or_2 (Operation_2, and_2_out, and_3_out, and_4_out);
  and and_5 (and_5_out, not_1_out, not_2_out);
  and and_6 (and_6_out, not_3_out, F5, F0);
  and and_7 (and_7_out, ALUop_2, ALUop_1);
  and and_8 (and_8_out, not_4_out, not_5_out, not_6_out, F3, F2, not_7_out, F0);
  and and_9 (and_9_out, not_8_out, not_9_out, ALUop_0);
  and and_10 (and_10_out, ALUop_2, ALUop_1);
  and and_11 (and_11_out, ALUop_3, not_10_out, F0);
  or or_3 (Operation_1, and_5_out, and_6_out, and_7_out);
  or or_4 (Operation_0, and_8_out, and_9_out, and_10_out, and_11_out);
endmodule

module control_0 (
  input  op_5,
  input  op_4,
  input  op_3,
  input  op_2,
  input  op_1,
  input  op_0,
  output RegDst,
  output Branch,
  output MemRead,
  output MemToReg,
  output MemWrite,
  output ALUsrc,
  output RegWrite
);

  wire and_5_out, and_6_out, and_7_out, not_1_out, not_2_out, not_3_out, not_4_out, not_5_out, not_6_out,
       not_7_out, not_8_out, not_9_out;

  not not_1 (not_1_out, op_5);
  not not_2 (not_2_out, op_3);
  not not_3 (not_3_out, op_5);
  not not_4 (not_4_out, op_3);
  not not_5 (not_5_out, op_3);
  and and_1 (MemWrite, op_5, op_3);
  or or_1 (ALUsrc, op_3, op_5);
  not not_6 (not_6_out, op_3);
  not not_7 (not_7_out, op_2);
  not not_8 (not_8_out, op_5);
  not not_9 (not_9_out, op_3);
  and and_2 (RegDst, not_1_out, not_2_out);
  and and_3 (Branch, not_3_out, not_4_out, op_2);
  and and_4 (MemRead, op_5, not_5_out);
  and and_5 (and_5_out, not_6_out, not_7_out);
  and and_6 (and_6_out, not_8_out, op_3);
  and and_7 (and_7_out, op_5, not_9_out);
  or or_2 (RegWrite, and_5_out, and_6_out, and_7_out);

  assign MemToReg = op_5;
endmodule

module control_1 (
  input  op_5,
  input  op_4,
  input  op_3,
  input  op_2,
  input  op_1,
  input  op_0,
  output ALUop_3,
  output ALUop_2,
  output ALUop_1,
  output ALUop_0
);

  wire and_1_out, and_2_out, and_3_out, and_4_out, and_5_out, and_6_out, and_7_out, and_8_out, and_9_out,
       and_10_out, and_11_out, and_12_out, and_13_out, and_14_out, and_15_out, and_16_out, and_17_out,
       and_18_out, and_19_out, and_20_out, and_21_out, and_22_out, and_23_out, and_24_out, and_25_out,
       not_1_out, not_2_out, not_3_out, not_4_out, not_5_out, not_6_out, not_7_out, not_8_out, not_9_out,
       not_10_out, not_11_out, not_12_out, not_13_out, not_14_out, not_15_out, not_16_out, not_17_out,
       not_18_out, not_19_out, not_20_out, not_21_out, not_22_out, or_3_out, or_4_out, or_6_out;

  not not_1 (not_1_out, op_5);
  not not_2 (not_2_out, op_3);
  not not_3 (not_3_out, op_3);
  not not_4 (not_4_out, op_1);
  not not_5 (not_5_out, op_5);
  not not_6 (not_6_out, op_4);
  not not_7 (not_7_out, op_5);
  not not_8 (not_8_out, op_3);
  and and_1 (and_1_out, not_1_out, not_2_out);
  not not_9 (not_9_out, op_2);
  and and_2 (and_2_out, not_3_out, op_2);
  and and_3 (and_3_out, op_1, op_0);
  not not_10 (not_10_out, op_0);
  and and_4 (and_4_out, op_2, not_4_out);
  not not_11 (not_11_out, op_3);
  not not_12 (not_12_out, op_1);
  not not_13 (not_13_out, op_3);
  and and_5 (and_5_out, not_5_out, not_6_out);
  not not_14 (not_14_out, op_1);
  not not_15 (not_15_out, op_0);
  not not_16 (not_16_out, op_5);
  not not_17 (not_17_out, op_2);
  not not_18 (not_18_out, op_0);
  and and_6 (and_6_out, not_7_out, op_2);
  not not_19 (not_19_out, op_0);
  and and_7 (and_7_out, not_8_out, op_2);
  not not_20 (not_20_out, op_5);
  and and_8 (and_8_out, and_1_out, not_9_out);
  and and_9 (and_9_out, and_2_out, and_3_out);
  and and_10 (and_10_out, op_1, not_10_out);
  and and_11 (and_11_out, and_4_out, op_0);
  and and_12 (and_12_out, not_11_out, not_12_out);
  and and_13 (and_13_out, not_13_out, op_1);
  not not_21 (not_21_out, op_0);
  and and_14 (and_14_out, and_5_out, op_3);
  and and_15 (and_15_out, not_14_out, not_15_out);
  and and_16 (and_16_out, not_16_out, op_3);
  and and_17 (and_17_out, not_17_out, not_18_out);
  and and_18 (and_18_out, and_6_out, not_19_out);
  and and_19 (and_19_out, and_7_out, op_1);
  and and_20 (and_20_out, not_20_out, op_3);
  not not_22 (not_22_out, op_0);
  or or_1 (ALUop_3, and_8_out, and_9_out);
  or or_2 (ALUop_2, and_10_out, and_11_out);
  and and_21 (and_21_out, and_12_out, op_0);
  and and_22 (and_22_out, and_13_out, not_21_out);
  and and_23 (and_23_out, and_14_out, and_15_out);
  and and_24 (and_24_out, and_16_out, and_17_out);
  or or_3 (or_3_out, and_18_out, and_19_out);
  and and_25 (and_25_out, and_20_out, not_22_out);
  or or_4 (or_4_out, and_21_out, and_22_out);
  or or_5 (ALUop_1, or_4_out, or_6_out);
  or or_6 (or_6_out, and_23_out, and_24_out);
  or or_7 (ALUop_0, or_3_out, and_25_out);
endmodule

module WireWidthExt_LCD_01 (
  input  [31:0] in_1,
  output [15:0] out_2
);


  assign out_2 = in_1[15:0];
endmodule

module WireWidthExt_LCD_02 (
  input  [31:0] in_1,
  output [6:0] out_2
);


  assign out_2 = in_1[22:16];
endmodule

module WireWidthExt_LCD_03 (
  input  [31:0] in_1,
  output [6:0] out_2
);


  assign out_2 = in_1[29:23];
endmodule

module Splitter_01 (
  input  [31:0] in_1,
  output out_2
);


  assign out_2 = in_1[0];
endmodule

module zero (
  input  [19:0] in_1,
  output out_2
);

  wire or_1_out, or_2_out, or_3_out;

  or or_1 (or_1_out, in_1[0], in_1[1], in_1[2], in_1[3], in_1[4]);
  or or_2 (or_2_out, in_1[5], in_1[6], in_1[7], in_1[8], in_1[9], in_1[10], in_1[11], in_1[12], in_1[13]);
  or or_3 (or_3_out, in_1[14], in_1[15], in_1[16], in_1[17], in_1[18], in_1[19]);
  nor nor_1 (out_2, or_1_out, or_2_out, or_3_out);
endmodule

module IDEX_Pipeline_Registers (
  input  RegDst,
  input  Branch,
  input  MemRead,
  input  MemToReg,
  input  [3:0] ALUOp,
  input  MemWrite,
  input  ALUSrc,
  input  RegWrite,
  input  Clock,
  input  Reset,
  output [1:0] WB,
  output [2:0] M,
  output RegDst_2,
  output [3:0] ALUOp_2,
  output ALUSrc_2
);

  Register #(.width(1)) u_RegDst (.D(RegDst), .Q(RegDst_2), .clk(Clock), .clr(Reset));  // open: en
  Register #(.width(1)) u_MemRead (.D(MemRead), .Q(M[0]), .clk(Clock), .clr(Reset));  // open: en
  Register #(.width(4)) u_ALUOp (.D(ALUOp), .Q(ALUOp_2), .clk(Clock), .clr(Reset));  // open: en
  Register #(.width(1)) u_ALUSrc (.D(ALUSrc), .Q(ALUSrc_2), .clk(Clock), .clr(Reset));  // open: en
  Register #(.width(1)) u_Branch (.D(Branch), .Q(M[2]), .clk(Clock), .clr(Reset));  // open: en
  Register #(.width(1)) u_MemToReg (.D(MemToReg), .Q(WB[1]), .clk(Clock), .clr(Reset));  // open: en
  Register #(.width(1)) u_MemWrite (.D(MemWrite), .Q(M[1]), .clk(Clock), .clr(Reset));  // open: en
  Register #(.width(1)) u_RegWrite (.D(RegWrite), .Q(WB[0]), .clk(Clock), .clr(Reset));  // open: en

  // Notes on the sheet:
  //   Inputs
  //   ID/EX Pipeline Registers
  //   Outputs
endmodule

module MEMWB_Pipeline_Registers (
  input  [1:0] WB,
  input  Clock,
  input  Reset,
  output RegWrite,
  output MemToReg
);

  Register #(.width(2)) register_1 (.D(WB), .Q({MemToReg, RegWrite}), .clk(Clock), .clr(Reset));  // open: en

  // Notes on the sheet:
  //   Inputs
  //   MEM/WB Pipeline Register
  //   Outputs
endmodule

module EXMEM_Pipeline_Registers (
  input  [1:0] WB,
  input  [2:0] M,
  input  Clock,
  input  Reset,
  output [1:0] WB_2,
  output MemRead,
  output MemWrite,
  output Branch
);

  Register #(.width(2)) register_1 (.D(WB), .Q(WB_2), .clk(Clock), .clr(Reset));  // open: en
  Register #(.width(3)) register_2 (.D(M), .Q({Branch, MemWrite, MemRead}), .clk(Clock), .clr(Reset));  // open: en
endmodule
