// Logisim project pipelined_datapath_project2.circ as structural Verilog: 13 circuits, main circuit Datapath
module Datapath (
  input  Reset,
  input  Clear
);

  wire and_1_out, and_2_out, and_3_out, and_4_out, Clock_out, control_1_alusrc, control_1_branch,
       control_1_memread, control_1_memtoreg, control_1_memwrite, control_1_regdst, control_1_regwrite,
       not_1_out, not_2_out, registerfile_1_p7, splitter_01_1_out_2, zero_1_out_2;
  wire [3:0] alucontrol_1_operation, control_1_aluop;
  wire [4:0] instructiondecode_1_rd, instructiondecode_1_rs, instructiondecode_1_rt,
       instructiondecode_1_shamt, multiplexer_1_out;
  wire [5:0] instructiondecode_1_funct, instructiondecode_1_op;
  wire [6:0] lcd_video_1_p4, lcd_video_1_p5;
  wire [15:0] instructiondecode_1_immediate, lcd_video_1_p6;
  wire [19:0] wirewidthext_1_wordaddress;
  wire [31:0] adder_1_out, branchaddress_1_branchaddress, memorydata_1_readdata, memorydata_1_tomemory,
       mips_alu_1_p5, mipsprogramrom_1_p2, multiplexer_2_out, multiplexer_3_out, multiplexer_5_out,
       register_1_q, register_2_q, registerfile_1_p1, registerfile_1_p8, signextend_1_out_2,
       wirewidthext_2_1_wordaddress;

  WireWidthExt_2 wirewidthext_2_1 (
    .ByteAddress(register_1_q), .WordAddress(wirewidthext_2_1_wordaddress));  // open: Unaligned
  Clock Clock (.out(Clock_out));
  Register #(.width(32)) register_1 (
    .D(multiplexer_3_out), .Q(register_1_q), .clk(Clock_out), .clr(Reset));  // open: en
  // MIPSProgramROM mipsprogramrom_1: pin names not known; wires that end beside it: wirewidthext_2_1_wordaddress, mipsprogramrom_1_p2
  // LCD_Video lcd_video_1: pin names not known; wires that end beside it: Reset, Clock_out, Clock_out, lcd_video_1_p4, lcd_video_1_p5, lcd_video_1_p6
  Adder #(.width(32)) adder_1 (.a(32'h4), .b(register_1_q), .out(adder_1_out));  // open: cin, cout
  InstructionDecode instructiondecode_1 (
    .Instruction(mipsprogramrom_1_p2), .op(instructiondecode_1_op), .rs(instructiondecode_1_rs),
    .rt(instructiondecode_1_rt), .rd(instructiondecode_1_rd), .shamt(instructiondecode_1_shamt),
    .funct(instructiondecode_1_funct), .immediate(instructiondecode_1_immediate));  // open: address
  Control control_1 (
    .op(instructiondecode_1_op), .RegDst(control_1_regdst), .Branch(control_1_branch),
    .MemRead(control_1_memread), .MemToReg(control_1_memtoreg), .ALUop(control_1_aluop),
    .MemWrite(control_1_memwrite), .ALUsrc(control_1_alusrc), .RegWrite(control_1_regwrite));
  Multiplexer #(.width(5), .enable("false")) multiplexer_1 (
    .in0(instructiondecode_1_rt), .in1(instructiondecode_1_rd), .out(multiplexer_1_out),
    .sel(control_1_regdst));
  not not_1 (not_1_out, Clock_out);
  SignExtend signextend_1 (.in_1(instructiondecode_1_immediate), .out_2(signextend_1_out_2));
  and and_1 (and_1_out, control_1_regwrite, not_1_out);
  // RegisterFile registerfile_1: pin names not known; wires that end beside it: registerfile_1_p1, and_1_out, and_1_out, multiplexer_1_out, instructiondecode_1_rs, instructiondecode_1_rt, registerfile_1_p7, registerfile_1_p8
  WireWidthExt_LCD_01 wirewidthext_lcd_01_1 (.out_2(lcd_video_1_p6), .in_1(multiplexer_5_out));
  WireWidthExt_LCD_02 wirewidthext_lcd_02_1 (.out_2(lcd_video_1_p5), .in_1(multiplexer_5_out));
  WireWidthExt_LCD_03 wirewidthext_lcd_03_1 (.out_2(lcd_video_1_p4), .in_1(multiplexer_5_out));
  ALUcontrol alucontrol_1 (
    .funct(instructiondecode_1_funct), .ALUop(control_1_aluop), .Operation(alucontrol_1_operation));
  Multiplexer #(.width(32), .enable("false")) multiplexer_2 (
    .in0(registerfile_1_p8), .in1(signextend_1_out_2), .out(multiplexer_2_out), .sel(control_1_alusrc));
  WireWidthExt wirewidthext_1 (.ByteAddress(mips_alu_1_p5), .WordAddress(wirewidthext_1_wordaddress));
  BranchAddress branchaddress_1 (
    .PC_4(adder_1_out), .Address(signextend_1_out_2), .BranchAddress(branchaddress_1_branchaddress));
  and and_2 (and_2_out, control_1_branch, splitter_01_1_out_2);
  // Mips_ALU mips_alu_1: pin names not known; wires that end beside it: registerfile_1_p7, multiplexer_2_out, alucontrol_1_operation, instructiondecode_1_shamt, mips_alu_1_p5
  and and_3 (and_3_out, not_1_out, control_1_memwrite);
  Multiplexer #(.width(32), .enable("false")) multiplexer_3 (
    .in0(adder_1_out), .in1(branchaddress_1_branchaddress), .out(multiplexer_3_out), .sel(and_2_out));
  Multiplexer #(.width(32), .enable("false")) multiplexer_4 (
    .in0(mips_alu_1_p5), .in1(memorydata_1_readdata), .out(registerfile_1_p1), .sel(control_1_memtoreg));
  MemoryData memorydata_1 (
    .WriteData(registerfile_1_p8), .FromMemory(memorydata_1_tomemory), .Write(control_1_memwrite),
    .Read(control_1_memread), .ReadData(memorydata_1_readdata), .ToMemory(memorydata_1_tomemory));
  Splitter_01 splitter_01_1 (.in_1(mips_alu_1_p5), .out_2(splitter_01_1_out_2));
  Multiplexer #(.width(32), .enable("false")) multiplexer_5 (
    .in0(register_2_q), .in1(memorydata_1_tomemory), .out(multiplexer_5_out), .sel(and_4_out));
  and and_4 (and_4_out, and_3_out, zero_1_out_2);
  Register #(.width(32)) register_2 (.D(multiplexer_5_out), .en(1'b1), .Q(register_2_q), .clk(not_2_out), .clr(Reset));
  not not_2 (not_2_out, and_4_out);
  // MIPS_RAM mips_ram_1: pin names not known; wires that end beside it: wirewidthext_1_wordaddress, registerfile_1_p8, 4'b1111, and_3_out, control_1_memread, Clear, memorydata_1_tomemory
  zero zero_1 (.in_1(wirewidthext_1_wordaddress), .out_2(zero_1_out_2));

  // Notes on the sheet:
  //   Instruction Memory
  //   PC
  //   Control
  //   Decode
  //   Registers
  //   Extend
  //   RGB
  //   Y
  //   X
  //   ALU control
  //   Branch
  //   ALU
  //   Data Memory
endmodule

module Control (
  input  [5:0] op,
  output RegDst,
  output Branch,
  output MemRead,
  output MemToReg,
  output [3:0] ALUop,
  output MemWrite,
  output ALUsrc,
  output RegWrite
);

  control_0 control_0_1 (
    .op_5(op[5]), .op_4(op[4]), .op_3(op[3]), .op_2(op[2]), .op_1(op[1]), .op_0(op[0]), .RegDst(RegDst),
    .Branch(Branch), .MemRead(MemRead), .MemToReg(MemToReg), .MemWrite(MemWrite), .ALUsrc(ALUsrc),
    .RegWrite(RegWrite));
  control_1 control_1_1 (
    .op_5(op[5]), .op_4(op[4]), .op_3(op[3]), .op_2(op[2]), .op_1(op[1]), .op_0(op[0]), .ALUop_3(ALUop[3]),
    .ALUop_2(ALUop[2]), .ALUop_1(ALUop[1]), .ALUop_0(ALUop[0]));
endmodule

module ALUcontrol (
  input  [5:0] funct,
  input  [3:0] ALUop,
  output [3:0] Operation
);

  ALUcontrol_0 alucontrol_0_1 (
    .ALUop_3(ALUop[3]), .ALUop_2(ALUop[2]), .ALUop_1(ALUop[1]), .ALUop_0(ALUop[0]), .F5(funct[5]),
    .F4(funct[4]), .F3(funct[3]), .F2(funct[2]), .F1(funct[1]), .F0(funct[0]), .Operation_3(Operation[3]),
    .Operation_2(Operation[2]), .Operation_1(Operation[1]), .Operation_0(Operation[0]));
endmodule

module WireWidthExt (
  input  [31:0] ByteAddress,
  output [19:0] WordAddress
);


  assign WordAddress = {{10{1'b0}}, ByteAddress[9:0]};
endmodule

module WireWidthExt_2 (
  input  [31:0] ByteAddress,
  output Unaligned,
  output [31:0] WordAddress
);

  nor nor_1 (Unaligned, ByteAddress[0], ByteAddress[1]);

  assign WordAddress = {{22{1'b0}}, ByteAddress[9:2], 2'b00};
endmodule

module ALUcontrol_0 (
  input  ALUop_3,
  input  ALUop_2,
  input  ALUop_1,
  input  ALUop_0,
  input  F5,
  input  F4,
  input  F3,
  input  F2,
  input  F1,
  input  F0,
  output Operation_3,
  output Operation_2,
  output Operation_1,
  output Operation_0
);

  wire and_1_out, and_2_out, and_3_out, and_4_out, and_5_out, and_6_out, and_7_out, and_8_out, and_9_out,
       and_10_out, and_11_out, not_1_out, not_2_out, not_3_out, not_4_out, not_5_out, not_6_out, not_7_out,
       not_8_out, not_9_out, not_10_out;

  and and_1 (and_1_out, ALUop_3, F5, F2);
  and and_2 (and_2_out, ALUop_2, ALUop_0);
  and and_3 (and_3_out, ALUop_3, F1);
  and and_4 (and_4_out, ALUop_3, ALUop_0);
  not not_1 (not_1_out, ALUop_3);
  not not_2 (not_2_out, ALUop_0);
  not not_3 (not_3_out, ALUop_0);
  not not_4 (not_4_out, ALUop_0);
  not not_5 (not_5_out, F5);
  not not_6 (not_6_out, F4);
  not not_7 (not_7_out, F1);
  not not_8 (not_8_out, ALUop_2);
  not not_9 (not_9_out, ALUop_1);
  not not_10 (not_10_out, F5);
  or or_1 (Operation_3, ALUop_0, ALUop_2, and_1_out);
  or or_2 (Operation_2, and_2_out, and_3_out, and_4_out);
  and and_5 (and_5_out, not_1_out, not_2_out);
  and and_6 (and_6_out, not_3_out, F5, F0);
  and and_7 (and_7_out, ALUop_2, ALUop_1);
  and and_8 (and_8_out, not_4_out, not_5_out, not_6_out, F3, F2, not_7_out, F0);
  and and_9 (and_9_out, not_8_out, not_9_out, ALUop_0);
  and and_10 (and_10_out, ALUop_2, ALUop_1);
  and and_11 (and_11_out, ALUop_3, not_10_out, F0);
  or or_3 (Operation_1, and_5_out, and_6_out, and_7_out);
  or or_4 (Operation_0, and_8_out, and_9_out, and_10_out, and_11_out);
endmodule

module control_0 (
  input  op_5,
  input  op_4,
  input  op_3,
  input  op_2,
  input  op_1,
  input  op_0,
  output RegDst,
  output Branch,
  output MemRead,
  output MemToReg,
  output MemWrite,
  output ALUsrc,
  output RegWrite
);

  wire and_5_out, and_6_out, and_7_out, not_1_out, not_2_out, not_3_out, not_4_out, not_5_out, not_6_out,
       not_7_out, not_8_out, not_9_out;

  not not_1 (not_1_out, op_5);
  not not_2 (not_2_out, op_3);
  not not_3 (not_3_out, op_5);
  not not_4 (not_4_out, op_3);
  not not_5 (not_5_out, op_3);
  and and_1 (MemWrite, op_5, op_3);
  or or_1 (ALUsrc, op_3, op_5);
  not not_6 (not_6_out, op_3);
  not not_7 (not_7_out, op_2);
  not not_8 (not_8_out, op_5);
  not not_9 (not_9_out, op_3);
  and and_2 (RegDst, not_1_out, not_2_out);
  and and_3 (Branch, not_3_out, not_4_out, op_2);
  and and_4 (MemRead, op_5, not_5_out);
  and and_5 (and_5_out, not_6_out, not_7_out);
  and and_6 (and_6_out, not_8_out, op_3);
  and and_7 (and_7_out, op_5, not_9_out);
  or or_2 (RegWrite, and_5_out, and_6_out, and_7_out);

  assign MemToReg = op_5;
endmodule

module control_1 (
  input  op_5,
  input  op_4,
  input  op_3,
  input  op_2,
  input  op_1,
  input  op_0,
  output ALUop_3,
  output ALUop_2,
  output ALUop_1,
  output ALUop_0
);

  wire and_1_out, and_2_out, and_3_out, and_4_out, and_5_out, and_6_out, and_7_out, and_8_out, and_9_out,
       and_10_out, and_11_out, and_12_out, and_13_out, and_14_out, and_15_out, and_16_out, and_17_out,
       and_18_out, and_19_out, and_20_out, and_21_out, and_22_out, and_23_out, and_24_out, and_25_out,
       not_1_out, not_2_out, not_3_out, not_4_out, not_5_out, not_6_out, not_7_out, not_8_out, not_9_out,
       not_10_out, not_11_out, not_12_out, not_13_out, not_14_out, not_15_out, not_16_out, not_17_out,
       not_18_out, not_19_out, not_20_out, not_21_out, not_22_out, or_3_out, or_4_out, or_6_out;

  not not_1 (not_1_out, op_5);
  not not_2 (not_2_out, op_3);
  not not_3 (not_3_out, op_3);
  not not_4 (not_4_out, op_1);
  not not_5 (not_5_out, op_5);
  not not_6 (not_6_out, op_4);
  not not_7 (not_7_out, op_5);
  not not_8 (not_8_out, op_3);
  and and_1 (and_1_out, not_1_out, not_2_out);
  not not_9 (not_9_out, op_2);
  and and_2 (and_2_out, not_3_out, op_2);
  and and_3 (and_3_out, op_1, op_0);
  not not_10 (not_10_out, op_0);
  and and_4 (and_4_out, op_2, not_4_out);
  not not_11 (not_11_out, op_3);
  not not_12 (not_12_out, op_1);
  not not_13 (not_13_out, op_3);
  and and_5 (and_5_out, not_5_out, not_6_out);
  not not_14 (not_14_out, op_1);
  not not_15 (not_15_out, op_0);
  not not_16 (not_16_out, op_5);
  not not_17 (not_17_out, op_2);
  not not_18 (not_18_out, op_0);
  and and_6 (and_6_out, not_7_out, op_2);
  not not_19 (not_19_out, op_0);
  and and_7 (and_7_out, not_8_out, op_2);
  not not_20 (not_20_out, op_5);
  and and_8 (and_8_out, and_1_out, not_9_out);
  and and_9 (and_9_out, and_2_out, and_3_out);
  and and_10 (and_10_out, op_1, not_10_out);
  and and_11 (and_11_out, and_4_out, op_0);
  and and_12 (and_12_out, not_11_out, not_12_out);
  and and_13 (and_13_out, not_13_out, op_1);
  not not_21 (not_21_out, op_0);
  and and_14 (and_14_out, and_5_out, op_3);
  and and_15 (and_15_out, not_14_out, not_15_out);
  and and_16 (and_16_out, not_16_out, op_3);
  and and_17 (and_17_out, not_17_out, not_18_out);
  and and_18 (and_18_out, and_6_out, not_19_out);
  and and_19 (and_19_out, and_7_out, op_1);
  and and_20 (and_20_out, not_20_out, op_3);
  not not_22 (not_22_out, op_0);
  or or_1 (ALUop_3, and_8_out, and_9_out);
  or or_2 (ALUop_2, and_10_out, and_11_out);
  and and_21 (and_21_out, and_12_out, op_0);
  and and_22 (and_22_out, and_13_out, not_21_out);
  and and_23 (and_23_out, and_14_out, and_15_out);
  and and_24 (and_24_out, and_16_out, and_17_out);
  or or_3 (or_3_out, and_18_out, and_19_out);
  and and_25 (and_25_out, and_20_out, not_22_out);
  or or_4 (or_4_out, and_21_out, and_22_out);
  or or_5 (ALUop_1, or_4_out, or_6_out);
  or or_6 (or_6_out, and_23_out, and_24_out);
  or or_7 (ALUop_0, or_3_out, and_25_out);
endmodule

module WireWidthExt_LCD_01 (
  input  [31:0] in_1,
  output [15:0] out_2
);


  assign out_2 = in_1[15:0];
endmodule

module WireWidthExt_LCD_02 (
  input  [31:0] in_1,
  output [6:0] out_2
);


  assign out_2 = in_1[22:16];
endmodule

module WireWidthExt_LCD_03 (
  input  [31:0] in_1,
  output [6:0] out_2
);


  assign out_2 = in_1[29:23];
endmodule

module Splitter_01 (
  input  [31:0] in_1,
  output out_2
);


  assign out_2 = in_1[0];
endmodule

module zero (
  input  [19:0] in_1,
  output out_2
);

  wire or_1_out, or_2_out, or_3_out;

  or or_1 (or_1_out, in_1[0], in_1[1], in_1[2], in_1[3], in_1[4]);
  or or_2 (or_2_out, in_1[5], in_1[6], in_1[7], in_1[8], in_1[9], in_1[10], in_1[11], in_1[12], in_1[13]);
  or or_3 (or_3_out, in_1[14], in_1[15], in_1[16], in_1[17], in_1[18], in_1[19]);
  nor nor_1 (out_2, or_1_out, or_2_out, or_3_out);
endmodule
